// Logisim project Enigma4700.circ as structural Verilog: 32 circuits, main circuit main
module main (
  input  in_1,
  input  in_2
);

  wire button_1_out, button_2_out, cu_1_hlt, mc_1_w, not_1_out, pow_1_cp, pow_1_res_2;
  wire [1:0] cu_1_a, cu_1_b, cu_1_bp, cu_1_c, cu_1_cs, cu_1_d_2, cu_1_di, cu_1_ds, cu_1_dst, cu_1_es,
       cu_1_ir, cu_1_mar, cu_1_mc, cu_1_mdr, cu_1_msr, cu_1_si, cu_1_sp, cu_1_src, cu_1_ss, cu_1_t1, cu_1_t2,
       cu_1_vec;
  wire [2:0] cu_1_op, cu_1_pc;
  wire [3:0] alu_1_psw, cu_1_alu, cu_1_cyc;
  wire [7:0] alu_1_s, pc_1_s, ram_1_data, reg_1_do, reg_1_s, reg_2_s, reg_3_s, reg_4_s, reg_5_s, reg_6_s,
       reg_7_s, reg_9_s, reg_11_s, reg_12_s, reg_13_s, reg_14_s, reg_15_s, reg_16_s, reg_17_s, reg_18_s,
       reg_19_s, reg_20_s, reg_21_s;
  wire [15:0] cu_1_a_2, reg_10_s;
  wire [31:0] rom_1_data;

  Button button_1 (.out(button_1_out));
  POW pow_1 (
    .RES(button_1_out), .POW(in_1), .MAN(in_2), .PUL(button_2_out), .HLT(cu_1_hlt), .CP(pow_1_cp),
    .RES_2(pow_1_res_2));
  Button button_2 (.out(button_2_out));
  // Probe on pow_1_res_2
  // Probe on pow_1_cp
  REG reg_1 (.DI(reg_1_do), .CLR(pow_1_res_2), .PR(1'b0), .CP(pow_1_cp), .IO(cu_1_cs), .DO(reg_1_do), .S(reg_1_s));
  MC mc_1 (.DI(ram_1_data), .W(mc_1_w), .CP(pow_1_cp), .IO(cu_1_mc), .DO(reg_1_do));  // open: S
  REG reg_2 (.DI(reg_1_do), .CLR(pow_1_res_2), .PR(1'b0), .CP(pow_1_cp), .IO(cu_1_ir), .DO(reg_1_do), .S(reg_2_s));
  // Probe on reg_2_s
  REG reg_3 (.DI(reg_1_do), .CLR(pow_1_res_2), .PR(1'b0), .CP(pow_1_cp), .IO(cu_1_dst), .DO(reg_1_do), .S(reg_3_s));
  // Probe on reg_3_s
  REG reg_4 (.DI(reg_1_do), .CLR(pow_1_res_2), .PR(1'b0), .CP(pow_1_cp), .IO(cu_1_src), .DO(reg_1_do), .S(reg_4_s));
  // Probe on reg_4_s
  // Probe on reg_1_s
  // Probe on reg_5_s
  REG reg_5 (.DI(reg_1_do), .CLR(pow_1_res_2), .PR(1'b0), .CP(pow_1_cp), .IO(cu_1_ds), .DO(reg_1_do), .S(reg_5_s));
  not not_1 (not_1_out, mc_1_w);
  REG reg_6 (.DI(reg_1_do), .CLR(pow_1_res_2), .PR(1'b0), .CP(pow_1_cp), .IO(cu_1_ss), .DO(reg_1_do), .S(reg_6_s));
  RAM #(.addrWidth(16), .bus("separate")) ram_1 (
    .addr(reg_10_s), .din(reg_1_do), .data(ram_1_data), .clk(pow_1_cp), .ld(not_1_out));  // open: str, sel, clr
  // Probe on reg_6_s
  REG reg_7 (.DI(reg_1_do), .CLR(pow_1_res_2), .PR(1'b0), .CP(pow_1_cp), .IO(cu_1_di), .DO(reg_1_do), .S(reg_7_s));
  REG reg_8 (
    .DI(reg_1_do), .CLR(pow_1_res_2), .PR(1'b0), .CP(pow_1_cp), .IO(cu_1_msr), .DO(reg_1_do),
    .S(reg_10_s[15:8]));
  CU cu_1 (
    .HLT(cu_1_hlt), .DI(cu_1_di), .CP(pow_1_cp), .SI(cu_1_si), .SP(cu_1_sp), .BP(cu_1_bp), .CS(cu_1_cs),
    .DS(cu_1_ds), .SS(cu_1_ss), .L1(reg_2_s), .ES(cu_1_es), .PSW(alu_1_psw), .CLR(pow_1_res_2),
    .d(rom_1_data), .SRC(cu_1_src), .DST(cu_1_dst), .IR(cu_1_ir), .a_2(cu_1_a_2), .ALU(cu_1_alu),
    .T2(cu_1_t2), .OP(cu_1_op), .T1(cu_1_t1), .PC(cu_1_pc), .VEC(cu_1_vec), .D_2(cu_1_d_2), .C(cu_1_c),
    .B(cu_1_b), .A(cu_1_a), .L2(reg_3_s), .L3(reg_4_s), .MSR(cu_1_msr), .MAR(cu_1_mar), .CYC(cu_1_cyc),
    .MDR(cu_1_mdr), .MC(cu_1_mc));
  // Probe on reg_7_s
  // Probe on reg_9_s
  REG reg_9 (.DI(reg_1_do), .CLR(pow_1_res_2), .PR(1'b0), .CP(pow_1_cp), .IO(cu_1_si), .DO(reg_1_do), .S(reg_9_s));
  REG reg_10 (
    .DI(reg_1_do), .CLR(pow_1_res_2), .PR(1'b0), .CP(pow_1_cp), .IO(cu_1_mar), .DO(reg_1_do),
    .S(reg_10_s[7:0]));
  // Probe on reg_12_s
  ROM #(.addrWidth(16), .dataWidth(32)) rom_1 (.addr(cu_1_a_2), .data(rom_1_data));  // open: sel
  REG reg_11 (.DI(reg_1_do), .CLR(pow_1_res_2), .PR(1'b0), .CP(pow_1_cp), .IO(cu_1_sp), .DO(reg_1_do), .S(reg_11_s));
  REG reg_12 (.DI(reg_1_do), .CLR(pow_1_res_2), .PR(1'b0), .CP(pow_1_cp), .IO(cu_1_mdr), .DO(reg_1_do), .S(reg_12_s));
  // Probe on reg_11_s
  REG reg_13 (.DI(reg_1_do), .CLR(pow_1_res_2), .PR(1'b0), .CP(pow_1_cp), .IO(cu_1_bp), .DO(reg_1_do), .S(reg_13_s));
  PC pc_1 (.CLR(pow_1_res_2), .PR(1'b0), .CP(pow_1_cp), .S(pc_1_s), .EN(cu_1_pc), .DI(reg_1_do), .DO(reg_1_do));
  // Probe on pc_1_s
  // Probe on cu_1_cyc
  // Probe on reg_13_s
  REG reg_14 (.CLR(pow_1_res_2), .PR(1'b0), .CP(pow_1_cp), .IO(cu_1_vec), .DO(reg_1_do), .S(reg_14_s));  // open: DI
  // Probe on alu_1_s
  // Probe on reg_14_s
  ALU alu_1 (
    .OP(cu_1_op), .PSW(alu_1_psw), .A(reg_18_s), .B(reg_16_s), .O(reg_1_do), .EN(cu_1_alu), .S(alu_1_s),
    .CLR(pow_1_res_2), .PR(1'b0), .CP(pow_1_cp));
  // Probe on reg_16_s
  REG reg_15 (.DI(reg_1_do), .CLR(pow_1_res_2), .PR(1'b0), .CP(pow_1_cp), .IO(cu_1_t1), .DO(reg_1_do), .S(reg_15_s));
  REG reg_16 (.DI(reg_1_do), .CLR(pow_1_res_2), .PR(1'b0), .CP(pow_1_cp), .IO(cu_1_b), .DO(reg_1_do), .S(reg_16_s));
  // Probe on reg_18_s
  // Probe on reg_15_s
  REG reg_17 (.DI(reg_1_do), .CLR(pow_1_res_2), .PR(1'b0), .CP(pow_1_cp), .IO(cu_1_t2), .DO(reg_1_do), .S(reg_17_s));
  REG reg_18 (.DI(reg_1_do), .CLR(pow_1_res_2), .PR(1'b0), .CP(pow_1_cp), .IO(cu_1_a), .DO(reg_1_do), .S(reg_18_s));
  // Probe on reg_20_s
  // Probe on reg_17_s
  REG reg_19 (.DI(reg_1_do), .CLR(pow_1_res_2), .PR(1'b0), .CP(pow_1_cp), .IO(cu_1_es), .S(reg_19_s));  // open: DO
  REG reg_20 (.DI(reg_1_do), .CLR(pow_1_res_2), .PR(1'b0), .CP(pow_1_cp), .IO(cu_1_c), .DO(reg_1_do), .S(reg_20_s));
  // Probe on reg_19_s
  REG reg_21 (.DI(reg_1_do), .CLR(pow_1_res_2), .PR(1'b0), .CP(pow_1_cp), .IO(cu_1_d_2), .DO(reg_1_do), .S(reg_21_s));
  // Probe on reg_21_s

  // Notes on the sheet:
  //   RES
  //   CLK
  //   CS
  //   IR
  //   DST
  //   SRC
  //   DS
  //   SS
  //   DI
  //   MSR
  //   SI
  //   MAR
  //   contents of rom_1 (hex, n*v repeats v):
  //   8040 1c0a4 8040 1c0c4 8040 1c0e4 10*80000000 8040 1c0a4 8040 1c0c4 8040 1c0e4 10*80000000 8040 1c0a4
  //   8040 1c0c4 8040 1c0e4 10*80000000 8040 1c0a4 8040 1c0c4 8040 1c0e4 10*80000000 8040 1c0a4 8040 1c0c4
  //   8040 1c0e4 10*80000000 8040 1c0a4 8040 1c0c4 8040 1c0e4 10*80000000 8040 1c0a4 8040 1c0c4 8040 1c0e4
  //   10*80000000 8040 1c0a4 8040 1c0c4 8040 1c0e4 10*80000000 8040 1c0a4 8040 1c0c4 8040 1c0e4
  //   10*80000000 8040 1c0a4 8040 1c0c4 8040 1c0e4 10*80000000 8040 1c0a4 8040 1c0c4 8040 1c0e4
  //   10*80000000 8040 1c0a4 8040 1c0c4 8040 1c0e4 10*80000000 8040 1c0a4 8040 1c0c4 8040 1c0e4
  //   10*80000000 8040 1c0a4 8040 1c0c4 8040 1c0e4 10*80000000 8040 1c0a4 8040 1c0c4 8040 1c0e4
  //   10*80000000 8040 1c0a4 8040 1c0c4 8040 1c0e4 10*80000000 8040 1c0a4 8040 1c0c4 8040 1c0e4
  //   10*80000000 8040 1c0a4 8040 1c0c4 8040 1c0e4 10*80000000 8040 1c0a4 8040 1c0c4 8040 1c0e4
  //   10*80000000 8040 1c0a4 8040 1c0c4 8040 1c0e4 10*80000000 8040 1c0a4 8040 1c0c4 8040 1c0e4
  //   10*80000000 8040 1c0a4 8040 1c0c4 8040 1c0e4 10*80000000 8040 1c0a4 8040 1c0c4 8040 1c0e4
  //   10*80000000 8040 1c0a4 8040 1c0c4 8040 1c0e4 10*80000000 8040 1c0a4 8040 1c0c4 8040 1c0e4
  //   10*80000000 8040 1c0a4 8040 1c0c4 8040 1c0e4 10*80000000 8040 1c0a4 8040 1c0c4 8040 1c0e4
  //   10*80000000 8040 1c0a4 8040 1c0c4 8040 1c0e4 10*80000000 8040 1c0a4 8040 1c0c4 8040 1c0e4
  //   10*80000000 8040 1c0a4 8040 1c0c4 8040 1c0e4 10*80000000 8040 1c0a4 8040 1c0c4 8040 1c0e4
  //   10*80000000 8040 1c0a4 8040 1c0c4 8040 1c0e4 10*80000000 8040 1c0a4 8040 1c0c4 8040 1c0e4
  //   10*80000000 8040 1c0a4 8040 1c0c4 8040 1c0e4 10*80000000 8040 1c0a4 8040 1c0c4 8040 1c0e4
  //   10*80000000 8040 1c0a4 8040 1c0c4 8040 1c0e4 10*80000000 8040 1c0a4 8040 1c0c4 8040 1c0e4
  //   10*80000000 8040 1c0a4 8040 1c0c4 8040 1c0e4 10*80000000 8040 1c0a4 8040 1c0c4 8040 1c0e4
  //   10*80000000 8040 1c0a4 8040 1c0c4 8040 1c0e4 10*80000000 8040 1c0a4 8040 1c0c4 8040 1c0e4
  //   10*80000000 8040 1c0a4 8040 1c0c4 8040 1c0e4 10*80000000 8040 1c0a4 8040 1c0c4 8040 1c0e4
  //   10*80000000 8040 1c0a4 8040 1c0c4 8040 1c0e4 10*80000000 8040 1c0a4 8040 1c0c4 8040 1c0e4
  //   10*80000000 8040 1c0a4 8040 1c0c4 8040 1c0e4 10*80000000 8040 1c0a4 8040 1c0c4 8040 1c0e4
  //   10*80000000 8040 1c0a4 8040 1c0c4 8040 1c0e4 10*80000000 8040 1c0a4 8040 1c0c4 8040 1c0e4
  //   10*80000000 8040 1c0a4 8040 1c0c4 8040 1c0e4 10*80000000 8040 1c0a4 8040 1c0c4 8040 1c0e4
  //   10*80000000 8040 1c0a4 8040 1c0c4 8040 1c0e4 10*80000000 8040 1c0a4 8040 1c0c4 8040 1c0e4
  //   10*80000000 8040 1c0a4 8040 1c0c4 8040 1c0e4 10*80000000 8040 1c0a4 8040 1c0c4 8040 1c0e4
  //   10*80000000 8040 1c0a4 8040 1c0c4 8040 1c0e4 10*80000000 8040 1c0a4 8040 1c0c4 8040 1c0e4
  //   10*80000000 8040 1c0a4 8040 1c0c4 8040 1c0e4 10*80000000 8040 1c0a4 8040 1c0c4 8040 1c0e4
  //   10*80000000 8040 1c0a4 8040 1c0c4 8040 1c0e4 10*80000000 8040 1c0a4 8040 1c0c4 8040 1c0e4
  //   10*80000000 8040 1c0a4 8040 1c0c4 8040 1c0e4 10*80000000 8040 1c0a4 8040 1c0c4 8040 1c0e4
  //   10*80000000 8040 1c0a4 8040 1c0c4 8040 1c0e4 10*80000000 8040 1c0a4 8040 1c0c4 8040 1c0e4
  //   10*80000000 8040 1c0a4 8040 1c0c4 8040 1c0e4 10*80000000 8040 1c0a4 8040 1c0c4 8040 1c0e4
  //   10*80000000 8040 1c0a4 8040 1c0c4 8040 1c0e4 10*80000000 8040 1c0a4 8040 1c0c4 8040 1c0e4
  //   10*80000000 8040 1c0a4 8040 1c0c4 8040 1c0e4 10*80000000 8040 1c0a4 8040 1c0c4 8040 1c0e4
  //   10*80000000 8040 1c0a4 8040 1c0c4 8040 1c0e4 10*80000000 8040 1c0a4 8040 1c0c4 8040 1c0e4
  //   10*80000000 8040 1c0a4 8040 1c0c4 8040 1c0e4 10*80000000 8040 1c0a4 8040 1c0c4 8040 1c0e4
  //   10*80000000 8040 1c0a4 8040 1c0c4 8040 1c0e4 10*80000000 8040 1c0a4 8040 1c0c4 8040 1c0e4
  //   10*80000000 8040 1c0a4 8040 1c0c4 8040 1c0e4 10*80000000 8040 1c0a4 8040 1c0c4 8040 1c0e4
  //   10*80000000 8040 1c0a4 8040 1c0c4 8040 1c0e4 10*80000000 8040 1c0a4 8040 1c0c4 8040 1c0e4
  //   10*80000000 8040 1c0a4 8040 1c0c4 8040 1c0e4 10*80000000 8040 1c0a4 8040 1c0c4 8040 1c0e4
  //   10*80000000 8040 1c0a4 8040 1c0c4 8040 1c0e4 10*80000000 8040 1c0a4 8040 1c0c4 8040 1c0e4
  //   10*80000000 8040 1c0a4 8040 1c0c4 8040 1c0e4 10*80000000 8040 1c0a4 8040 1c0c4 8040 1c0e4
  //   10*80000000 8040 1c0a4 8040 1c0c4 8040 1c0e4 10*80000000 8040 1c0a4 8040 1c0c4 8040 1c0e4 10*8000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
  //   SP
  //   MDR
  //   BP
  //   PC
  //   VEC
  //   B
  //   T1
  //   A
  //   T2
  //   C
  //   ES
  //   D
endmodule

module HA (
  input  A,
  input  B,
  output S,
  output C
);

  xor xor_1 (S, B, A);
  and and_1 (C, A, B);
endmodule

module FA (
  input  CI,
  input  A,
  input  B,
  output S,
  output CO
);

  wire ha_1_c, ha_2_c, ha_2_s;

  HA ha_1 (.A(CI), .B(ha_2_s), .S(S), .C(ha_1_c));
  HA ha_2 (.A(A), .B(B), .S(ha_2_s), .C(ha_2_c));
  or or_1 (CO, ha_1_c, ha_2_c);
endmodule

module _8BA (
  input  CI,
  input  [7:0] A,
  input  [7:0] B,
  output [7:0] S,
  output CO
);

  wire fa_2_co, fa_3_co, fa_4_co, fa_5_co, fa_6_co, fa_7_co, fa_8_co;

  FA fa_1 (.CI(fa_2_co), .A(A[7]), .B(B[7]), .S(S[7]), .CO(CO));
  FA fa_2 (.CI(fa_3_co), .A(A[6]), .B(B[6]), .S(S[6]), .CO(fa_2_co));
  FA fa_3 (.CI(fa_4_co), .A(A[5]), .B(B[5]), .S(S[5]), .CO(fa_3_co));
  FA fa_4 (.CI(fa_6_co), .A(A[4]), .B(B[4]), .S(S[4]), .CO(fa_4_co));
  FA fa_5 (.CI(fa_7_co), .A(A[2]), .B(B[2]), .S(S[2]), .CO(fa_5_co));
  FA fa_6 (.CI(fa_5_co), .A(A[3]), .B(B[3]), .S(S[3]), .CO(fa_6_co));
  FA fa_7 (.CI(fa_8_co), .A(A[1]), .B(B[1]), .S(S[1]), .CO(fa_7_co));
  FA fa_8 (.CI(CI), .A(A[0]), .B(B[0]), .S(S[0]), .CO(fa_8_co));
endmodule

module INV (
  input  [7:0] in_1,
  input  in_2,
  output [7:0] out_3
);

  xor xor_1 (out_3[7], in_2, in_1[7]);
  xor xor_2 (out_3[6], in_2, in_1[6]);
  xor xor_3 (out_3[5], in_2, in_1[5]);
  xor xor_4 (out_3[4], in_2, in_1[4]);
  xor xor_5 (out_3[3], in_2, in_1[3]);
  xor xor_6 (out_3[2], in_2, in_1[2]);
  xor xor_7 (out_3[1], in_2, in_1[1]);
  xor xor_8 (out_3[0], in_2, in_1[0]);
endmodule

module R_S (
  input  CLR,
  input  R,
  input  S,
  input  PR,
  output Q,
  output Q_prime
);

  nor nor_1 (Q, CLR, R, Q_prime);
  nor nor_2 (Q_prime, Q, S, PR);
endmodule

module D (
  input  CLR,
  input  EN,
  input  D,
  input  PR,
  output Q,
  output Q_prime
);

  wire and_1_out, and_2_out, not_1_out;

  not not_1 (not_1_out, D);
  and and_1 (and_1_out, not_1_out, EN);
  and and_2 (and_2_out, EN, D);
  R_S r_s_1 (.R(and_1_out), .S(and_2_out), .CLR(CLR), .PR(PR), .Q(Q), .Q_prime(Q_prime));
endmodule

module D_2 (
  input  CLR,
  input  D,
  input  CP,
  input  PR,
  output Q,
  output Q_prime
);

  wire d_1_q, not_1_out;

  D d_1 (.EN(not_1_out), .D(D), .Q(d_1_q), .PR(PR), .CLR(CLR));  // open: Q_prime
  not not_1 (not_1_out, CP);
  D d_2 (.EN(CP), .D(d_1_q), .Q(Q), .Q_prime(Q_prime), .PR(PR), .CLR(CLR));
endmodule

module T (
  input  CLR,
  input  CP,
  input  PR,
  output Q,
  output Q_prime
);

  D_2 d_1 (.D(Q_prime), .CP(CP), .CLR(CLR), .PR(PR), .Q(Q), .Q_prime(Q_prime));
endmodule

module _8CT (
  input  CLR,
  input  CP,
  input  EN,
  input  PR,
  output [7:0] O
);

  wire and_1_out, t_1_q_prime, t_2_q_prime, t_3_q_prime, t_4_q_prime, t_5_q_prime, t_6_q_prime, t_7_q_prime;

  and and_1 (and_1_out, CP, EN);
  T t_1 (.CP(and_1_out), .CLR(CLR), .PR(PR), .Q(O[0]), .Q_prime(t_1_q_prime));
  T t_2 (.CP(t_1_q_prime), .CLR(CLR), .PR(PR), .Q(O[1]), .Q_prime(t_2_q_prime));
  T t_3 (.CP(t_2_q_prime), .CLR(CLR), .PR(PR), .Q(O[2]), .Q_prime(t_3_q_prime));
  T t_4 (.CP(t_3_q_prime), .CLR(CLR), .PR(PR), .Q(O[3]), .Q_prime(t_4_q_prime));
  T t_5 (.CP(t_4_q_prime), .CLR(CLR), .PR(PR), .Q(O[4]), .Q_prime(t_5_q_prime));
  T t_6 (.CP(t_5_q_prime), .CLR(CLR), .PR(PR), .Q(O[5]), .Q_prime(t_6_q_prime));
  T t_7 (.CP(t_6_q_prime), .CLR(CLR), .PR(PR), .Q(O[6]), .Q_prime(t_7_q_prime));
  T t_8 (.CP(t_7_q_prime), .CLR(CLR), .PR(PR), .Q(O[7]));  // open: Q_prime
endmodule

module BYTE (
  input  [7:0] DI,
  input  CLR,
  input  PR,
  input  CP,
  output [7:0] DO
);

  D_2 d_1 (.D(DI[0]), .CP(CP), .CLR(CLR), .PR(PR), .Q(DO[0]));  // open: Q_prime
  D_2 d_2 (.D(DI[1]), .CP(CP), .CLR(CLR), .PR(PR), .Q(DO[1]));  // open: Q_prime
  D_2 d_3 (.D(DI[2]), .CP(CP), .CLR(CLR), .PR(PR), .Q(DO[2]));  // open: Q_prime
  D_2 d_4 (.D(DI[3]), .CP(CP), .CLR(CLR), .PR(PR), .Q(DO[3]));  // open: Q_prime
  D_2 d_5 (.D(DI[4]), .CP(CP), .CLR(CLR), .PR(PR), .Q(DO[4]));  // open: Q_prime
  D_2 d_6 (.D(DI[6]), .CP(CP), .CLR(CLR), .PR(PR), .Q(DO[6]));  // open: Q_prime
  D_2 d_7 (.D(DI[5]), .CP(CP), .CLR(CLR), .PR(PR), .Q(DO[5]));  // open: Q_prime
  D_2 d_8 (.D(DI[7]), .CP(CP), .CLR(CLR), .PR(PR), .Q(DO[7]));  // open: Q_prime
endmodule

module GATE (
  input  [7:0] DI,
  input  EN,
  output [7:0] DO
);

  assign DO[7] = EN ? DI[7] : 1'bz;  // Controlled_Buffer controlled_buffer_1
  assign DO[6] = EN ? DI[6] : 1'bz;  // Controlled_Buffer controlled_buffer_2
  assign DO[4] = EN ? DI[4] : 1'bz;  // Controlled_Buffer controlled_buffer_3
  assign DO[5] = EN ? DI[5] : 1'bz;  // Controlled_Buffer controlled_buffer_4
  assign DO[3] = EN ? DI[3] : 1'bz;  // Controlled_Buffer controlled_buffer_5
  assign DO[2] = EN ? DI[2] : 1'bz;  // Controlled_Buffer controlled_buffer_6
  assign DO[1] = EN ? DI[1] : 1'bz;  // Controlled_Buffer controlled_buffer_7
  assign DO[0] = EN ? DI[0] : 1'bz;  // Controlled_Buffer controlled_buffer_8
endmodule

module REG (
  input  [7:0] DI,
  input  CLR,
  input  PR,
  input  CP,
  input  [1:0] IO,
  output [7:0] S,
  output [7:0] DO
);

  wire and_1_out, and_2_out, not_1_out;

  and and_1 (and_1_out, CP, IO[1], IO[0]);
  BYTE byte_1 (.DI(DI), .CLR(CLR), .PR(PR), .CP(and_1_out), .DO(S));
  GATE gate_1 (.DI(S), .EN(and_2_out), .DO(DO));
  and and_2 (and_2_out, not_1_out, IO[1]);
  not not_1 (not_1_out, IO[0]);
endmodule

module _8x1 (
  input  [7:0] DI,
  input  CLR,
  input  PR,
  input  CP,
  input  WE,
  input  [2:0] A,
  input  CS,
  output [7:0] DO
);

  wire [7:0] n38dec_1_o;

  _38DEC u_38dec_1 (.A2(A[2]), .A1(A[1]), .A0(A[0]), .EN(CS), .O(n38dec_1_o));
  REG reg_1 (.DI(DI), .CLR(CLR), .PR(PR), .CP(CP), .IO({n38dec_1_o[7], WE}), .DO(DO));  // open: S
  REG reg_2 (.DI(DI), .CLR(CLR), .PR(PR), .CP(CP), .IO({n38dec_1_o[6], WE}), .DO(DO));  // open: S
  REG reg_3 (.DI(DI), .CLR(CLR), .PR(PR), .CP(CP), .IO({n38dec_1_o[5], WE}), .DO(DO));  // open: S
  REG reg_4 (.DI(DI), .CLR(CLR), .PR(PR), .CP(CP), .IO({n38dec_1_o[4], WE}), .DO(DO));  // open: S
  REG reg_5 (.DI(DI), .CLR(CLR), .PR(PR), .CP(CP), .IO({n38dec_1_o[3], WE}), .DO(DO));  // open: S
  REG reg_6 (.DI(DI), .CLR(CLR), .PR(PR), .IO({n38dec_1_o[2], WE}), .DO(DO));  // open: CP, S
  REG reg_7 (.DI(DI), .CLR(CLR), .PR(PR), .CP(CP), .IO({n38dec_1_o[1], WE}), .DO(DO));  // open: S
  REG reg_8 (.DI(DI), .CLR(CLR), .PR(PR), .CP(CP), .IO({n38dec_1_o[0], WE}), .DO(DO));  // open: S
endmodule

module _38DEC (
  input  A2,
  input  A1,
  input  A0,
  input  EN,
  output [7:0] O
);

  wire not_1_out, not_2_out, not_3_out;

  not not_1 (not_1_out, A2);
  not not_2 (not_2_out, A1);
  not not_3 (not_3_out, A0);
  and and_1 (O[6], A2, A1, not_3_out, EN);
  and and_2 (O[7], A2, A1, A0, EN);
  and and_3 (O[5], A2, not_2_out, A0, EN);
  and and_4 (O[4], A2, not_2_out, not_3_out, EN);
  and and_5 (O[2], not_1_out, A1, not_3_out, EN);
  and and_6 (O[3], not_1_out, A1, A0, EN);
  and and_7 (O[1], not_1_out, not_2_out, A0, EN);
  and and_8 (O[0], not_1_out, not_2_out, not_3_out, EN);
endmodule

module _2x8 (
  input  [15:0] DI,
  input  CLR,
  input  PR,
  input  CP,
  input  [2:0] A,
  input  WE,
  input  CS,
  output [15:0] DO
);

  _8x1 u_8x1_1 (.DI(DI[15:8]), .CLR(CLR), .PR(PR), .CP(CP), .A(A), .CS(CS), .DO(DO[15:8]), .WE(WE));
  _8x1 u_8x1_2 (.DI(DI[7:0]), .CLR(CLR), .PR(PR), .CP(CP), .A(A), .CS(CS), .DO(DO[7:0]), .WE(WE));
endmodule

module _3CT (
  input  CLR,
  input  EN,
  input  PR,
  input  CP,
  output [2:0] O
);

  wire [7:3] n8ct_1_o;

  _8CT u_8ct_1 (.O({n8ct_1_o, O}), .CLR(CLR), .CP(CP), .PR(PR), .EN(EN));
endmodule

module ALU (
  input  [7:0] A,
  input  [7:0] B,
  input  [2:0] OP,
  input  [3:0] EN,
  input  CLR,
  input  PR,
  input  CP,
  output [7:0] S,
  output [7:0] O,
  output [3:0] PSW
);

  wire and_1_out, and_2_out, n8ba_1_co, n8ba_2_co;
  wire [1:0] or_1_out;
  wire [7:0] inv_1_out_3, inv_2_out_3, n8and_1_o, n8ba_1_s, n8ba_2_s, n8or_1_o, n8xor_1_o, n38dec_1_o;
  wire [7:4] reg_1_s;

  _38DEC u_38dec_1 (.A2(OP[2]), .A1(OP[1]), .A0(OP[0]), .EN(1'b1), .O(n38dec_1_o));
  _8BA u_8ba_1 (.CI(1'b0), .A(A), .B(B), .S(n8ba_1_s), .CO(n8ba_1_co));
  GATE gate_1 (.DI(n8ba_1_s), .EN(n38dec_1_o[0]), .DO(S));
  _8BA u_8ba_2 (.CI(1'b1), .A(A), .B(inv_1_out_3), .S(n8ba_2_s), .CO(n8ba_2_co));
  GATE gate_2 (.DI(n8ba_2_s), .EN(n38dec_1_o[1]), .DO(S));
  and and_1 (and_1_out, n38dec_1_o[0], n8ba_1_co);
  INV inv_1 (.in_1(B), .in_2(1'b1), .out_3(inv_1_out_3));
  and and_2 (and_2_out, n38dec_1_o[1], n8ba_2_co);
  nor nor_1 (or_1_out[1], S[0], S[1], S[2], S[3], S[4], S[5], S[6], S[7]);
  _8AND u_8and_1 (.A(A), .B(B), .O(n8and_1_o));
  GATE gate_3 (.DI(n8and_1_o), .EN(n38dec_1_o[2]), .DO(S));
  or or_1 (or_1_out[0], and_2_out, and_1_out);
  _8OR u_8or_1 (.A(A), .B(B), .O(n8or_1_o));
  GATE gate_4 (.DI(n8xor_1_o), .EN(n38dec_1_o[4]), .DO(S));
  GATE gate_5 (.DI(n8or_1_o), .EN(n38dec_1_o[3]), .DO(S));
  REG reg_1 (
    .DI({{5{1'b0}}, S[0], or_1_out}), .CLR(CLR), .PR(PR), .CP(CP), .IO(2'b01), .S({reg_1_s, PSW}));  // open: DO
  _8XOR u_8xor_1 (.A(A), .B(B), .O(n8xor_1_o));
  GATE gate_6 (.DI(inv_2_out_3), .EN(n38dec_1_o[5]), .DO(S));
  INV inv_2 (.in_1(A), .in_2(1'b1), .out_3(inv_2_out_3));
  GATE gate_7 (.DI(S), .EN(EN[0]), .DO(O));
endmodule

module POW (
  input  RES,
  input  POW,
  input  MAN,
  input  PUL,
  input  HLT,
  output CP,
  output RES_2
);

  wire and_1_out, and_2_out, and_3_out, clock_1_out, not_1_out, not_2_out, not_3_out, not_4_out, not_5_out;

  Clock clock_1 (.out(clock_1_out));
  not not_1 (not_1_out, RES);
  not not_2 (not_2_out, POW);
  not not_3 (not_3_out, MAN);
  not not_4 (not_4_out, PUL);
  not not_5 (not_5_out, HLT);
  and and_1 (and_1_out, POW, not_1_out, not_3_out, not_5_out, clock_1_out);
  and and_2 (and_2_out, POW, not_1_out, MAN, not_5_out, PUL);
  or or_1 (CP, and_1_out, and_2_out);
  and and_3 (and_3_out, POW, RES);
  or or_2 (RES_2, and_3_out, not_2_out);

  // Notes on the sheet:
  //   RESET
  //   POWER
  //   MANUAL
  //   PULSE
  //   HALT
  //   CLOCK
endmodule

module PC (
  input  [7:0] DI,
  input  CLR,
  input  PR,
  input  CP,
  input  [2:0] EN,
  output [7:0] DO,
  output [7:0] S
);

  wire not_1_out;
  wire [7:0] gate_1_do, n8ba_1_s;

  GATE gate_1 (.DI(DI), .EN(not_1_out), .DO(gate_1_do));
  not not_1 (not_1_out, EN[2]);
  REG reg_1 (.DI(gate_1_do), .CLR(CLR), .PR(PR), .CP(CP), .IO(EN[1:0]), .DO(DO), .S(S));
  _8BA u_8ba_1 (.CI(1'b0), .A(S), .B(8'h1), .S(n8ba_1_s));  // open: CO
  GATE gate_2 (.DI(n8ba_1_s), .EN(EN[2]), .DO(gate_1_do));
endmodule

module MC (
  input  [7:0] DI,
  input  CP,
  input  [1:0] IO,
  output W,
  output [7:0] S,
  output [7:0] DO
);

  wire and_2_out, not_1_out;

  and and_1 (W, CP, IO[0], IO[1]);
  GATE gate_1 (.DI(DI), .EN(and_2_out), .DO(DO));
  and and_2 (and_2_out, not_1_out, IO[1]);
  not not_1 (not_1_out, IO[0]);

  assign S = DI;
endmodule

module EW (
  input  [7:0] in_1,
  input  in_2,
  output [7:0] DO
);

  GATE gate_1 (.DI(in_1), .EN(in_2), .DO(DO));
endmodule

module _8AND (
  input  [7:0] A,
  input  [7:0] B,
  output [7:0] O
);

  and and_1 (O[0], B[0], A[0]);
  and and_2 (O[1], B[1], A[1]);
  and and_3 (O[2], B[2], A[2]);
  and and_4 (O[3], B[3], A[3]);
  and and_5 (O[4], B[4], A[4]);
  and and_6 (O[5], B[5], A[5]);
  and and_7 (O[6], B[6], A[6]);
  and and_8 (O[7], B[7], A[7]);
endmodule

module _8OR (
  input  [7:0] A,
  input  [7:0] B,
  output [7:0] O
);

  or or_1 (O[0], B[0], A[0]);
  or or_2 (O[1], B[1], A[1]);
  or or_3 (O[2], B[2], A[2]);
  or or_4 (O[3], B[3], A[3]);
  or or_5 (O[4], B[4], A[4]);
  or or_6 (O[5], B[5], A[5]);
  or or_7 (O[6], B[6], A[6]);
  or or_8 (O[7], B[7], A[7]);
endmodule

module _8XOR (
  input  [7:0] A,
  input  [7:0] B,
  output [7:0] O
);

  xor xor_1 (O[0], B[0], A[0]);
  xor xor_2 (O[1], B[1], A[1]);
  xor xor_3 (O[2], B[2], A[2]);
  xor xor_4 (O[3], B[3], A[3]);
  xor xor_5 (O[4], B[4], A[4]);
  xor xor_6 (O[5], B[5], A[5]);
  xor xor_7 (O[6], B[6], A[6]);
  xor xor_8 (O[7], B[7], A[7]);
endmodule

module RC (
  input  [4:0] W,
  input  [4:0] R,
  output [1:0] CS,
  output [1:0] A,
  output [1:0] DS,
  output [1:0] B,
  output [1:0] MSR,
  output [1:0] SS,
  output [1:0] C,
  output [1:0] MAR,
  output [1:0] ES,
  output [1:0] D,
  output [1:0] MDR,
  output [1:0] VEC,
  output [1:0] DI,
  output [1:0] MC,
  output [1:0] T1,
  output [1:0] SI,
  output [1:0] IR,
  output [1:0] T2,
  output [1:0] SP,
  output [1:0] DST,
  output [1:0] BP,
  output [1:0] SRC
);

  wire [31:0] n32xor_1_out_3, n532dec_1_d, n532dec_2_d;

  _532DEC u_532dec_1 (
    .A(W),
    .D({n532dec_1_d[31:23], T2[0], T1[0], VEC[0], ES[0], SS[0], DS[0], CS[0], BP[0], SP[0], SI[0], DI[0], D[0], C[0], B[0], A[0], SRC[0], DST[0], IR[0], MC[0], MDR[0], MAR[0], MSR[0], n532dec_1_d[0]}));
  _532DEC u_532dec_2 (.A(R), .D(n532dec_2_d));
  _32XOR u_32xor_1 (
    .A({n532dec_1_d[31:23], T2[0], T1[0], VEC[0], ES[0], SS[0], DS[0], CS[0], BP[0], SP[0], SI[0], DI[0], D[0], C[0], B[0], A[0], SRC[0], DST[0], IR[0], MC[0], MDR[0], MAR[0], MSR[0], n532dec_1_d[0]}),
    .B(n532dec_2_d),
    .out_3({n32xor_1_out_3[31:23], T2[1], T1[1], VEC[1], ES[1], SS[1], DS[1], CS[1], BP[1], SP[1], SI[1], DI[1], D[1], C[1], B[1], A[1], SRC[1], DST[1], IR[1], MC[1], MDR[1], MAR[1], MSR[1], n32xor_1_out_3[0]}));
endmodule

module _532DEC (
  input  [4:0] A,
  output [31:0] D
);

  ROM #(.addrWidth(5), .dataWidth(32)) rom_1 (.addr(A), .data(D));  // open: sel

  // Notes on the sheet:
  //   contents of rom_1 (hex, n*v repeats v):
  //   1 2 4 8 10 20 40 80 100 200 400 800 1000 2000 4000 8000 10000 20000 40000 80000 100000 200000 400000
  //   800000 1000000 2000000 4000000 8000000 10000000 20000000 40000000 80000000
endmodule

module _32XOR (
  input  [31:0] A,
  input  [31:0] B,
  output [31:0] out_3
);

  _8XOR u_8xor_1 (.A(A[7:0]), .B(B[7:0]), .O(out_3[7:0]));
  _8XOR u_8xor_2 (.A(A[15:8]), .B(B[15:8]), .O(out_3[15:8]));
  _8XOR u_8xor_3 (.A(A[23:16]), .B(B[23:16]), .O(out_3[23:16]));
  _8XOR u_8xor_4 (.A(A[31:24]), .B(B[31:24]), .O(out_3[31:24]));
endmodule

module RWC (
  input  [4:0] DC,
  input  [4:0] SC,
  input  [7:0] D,
  input  DR,
  input  DW,
  input  [7:0] S,
  input  SW,
  input  SR,
  output [4:0] W,
  output [4:0] R
);

  wire [7:0] n821s_1_s, n821s_3_s;
  wire [7:5] n821s_2_s, n821s_4_s;

  _821S u_821s_1 (.A({3'b000, DC}), .B(D), .WN(DW), .S(n821s_1_s));
  _821S u_821s_2 (.A(n821s_1_s), .B(S), .WN(SW), .S({n821s_2_s, W}));
  _821S u_821s_3 (.A({3'b000, SC}), .B(D), .WN(DR), .S(n821s_3_s));
  _821S u_821s_4 (.A(n821s_3_s), .B(S), .WN(SR), .S({n821s_4_s, R}));
endmodule

module _21S (
  input  A,
  input  B,
  input  in_3,
  output out_4
);

  wire and_1_out, and_2_out, not_1_out;

  not not_1 (not_1_out, in_3);
  and and_1 (and_1_out, in_3, A);
  nor nor_1 (out_4, and_1_out, and_2_out);
  and and_2 (and_2_out, not_1_out, B);
endmodule

module _821S (
  input  [7:0] A,
  input  [7:0] B,
  input  WN,
  output [7:0] S
);

  _21S u_21s_1 (.in_3(WN), .A(B[0]), .B(A[7]), .out_4(S[7]));
  _21S u_21s_2 (.in_3(WN), .A(B[1]), .B(A[6]), .out_4(S[6]));
  _21S u_21s_3 (.in_3(WN), .A(B[2]), .B(A[5]), .out_4(S[5]));
  _21S u_21s_4 (.in_3(WN), .A(B[3]), .B(A[4]), .out_4(S[4]));
  _21S u_21s_5 (.in_3(WN), .A(B[4]), .B(A[3]), .out_4(S[3]));
  _21S u_21s_6 (.in_3(WN), .A(B[5]), .B(A[2]), .out_4(S[2]));
  _21S u_21s_7 (.in_3(WN), .A(B[6]), .B(A[1]), .out_4(S[1]));
  _21S u_21s_8 (.in_3(WN), .A(B[7]), .B(A[0]), .out_4(S[0]));
endmodule

module CU (
  input  [31:0] d,
  input  [7:0] L2,
  input  [7:0] L3,
  input  CLR,
  input  CP,
  input  [3:0] PSW,
  input  [7:0] L1,
  output HLT,
  output [3:0] ALU,
  output [2:0] OP,
  output [2:0] PC,
  output [1:0] SRC,
  output [1:0] DST,
  output [1:0] IR,
  output [1:0] DI,
  output [1:0] MSR,
  output [1:0] SI,
  output [1:0] SP,
  output [1:0] MAR,
  output [1:0] BP,
  output [3:0] CYC,
  output [1:0] CS,
  output [1:0] MDR,
  output [1:0] DS,
  output [1:0] SS,
  output [1:0] MC,
  output [1:0] ES,
  output [1:0] T2,
  output [1:0] T1,
  output [1:0] VEC,
  output [1:0] D_2,
  output [1:0] C,
  output [1:0] B,
  output [1:0] A,
  output [15:0] a_2
);

  wire not_1_out;
  wire [2:0] rom_1_data;
  wire [4:0] rwc_1_r, rwc_1_w;
  wire [7:4] pc_1_s;

  not not_1 (not_1_out, CP);
  PC pc_1 (.CLR(CLR), .PR(1'b0), .CP(not_1_out), .S({pc_1_s, a_2[3:0]}), .EN(rom_1_data), .DI({8{1'b0}}));  // open: DO
  ROM #(.addrWidth(2), .dataWidth(3)) rom_1 (.addr({1'b0, d[30]}), .data(rom_1_data));  // open: sel
  RWC rwc_1 (
    .DR(d[12]), .DW(d[13]), .SW(d[11]), .SR(d[10]), .D(L2), .S(L3), .DC(d[9:5]), .SC(d[4:0]), .W(rwc_1_w),
    .R(rwc_1_r));
  RC rc_1 (
    .W(rwc_1_w), .R(rwc_1_r), .CS(CS), .A(A), .DS(DS), .B(B), .MSR(MSR), .SS(SS), .C(C), .MAR(MAR), .ES(ES),
    .D(D_2), .MDR(MDR), .VEC(VEC), .DI(DI), .MC(MC), .T1(T1), .SI(SI), .IR(IR), .T2(T2), .SP(SP), .DST(DST),
    .BP(BP), .SRC(SRC));

  assign a_2[15:4] = {L1, PSW};
  assign ALU = d[23:20];
  assign CYC = a_2[3:0];
  assign HLT = d[31];
  assign OP = d[19:17];
  assign PC = d[16:14];

  // Notes on the sheet:
  //   contents of rom_1 (hex, n*v repeats v):
  //   7 3
endmodule
